# Fritzing sketch MACAv1.1 (saved by Fritzing 0.9.3b)
circuit board: 5.3cm x 5.4cm
breadboards: 1

parts:
  Componente2 = Arduino Ethernet Shield (Rev3)
  DHT = Humidity and Temperature Sensor RHT03
  R1 = Resistor [tolerance=±5% resistance=220 package=THT]
  R2 = Resistor [tolerance=±5% resistance=100 package=THT]
  R3 = Resistor [tolerance=±5% resistance=22 package=THT]
  R4 = Resistor [tolerance=±5% resistance=33 package=THT]
  R5 = Resistor [tolerance=±5% resistance=39 package=THT]
  R6 = Resistor [tolerance=±5% resistance=39 package=THT]
  R7 = Resistor [tolerance=±5% resistance=39 package=THT]
  RL2 = Resistor [tolerance=±5% resistance=22k package=THT]
  RL3 = Resistor [tolerance=±5% resistance=22k package=THT]
  RL1 = Resistor [tolerance=±5% resistance=22k package=THT]

nets:
  N1: Componente2.SPI/D12, DHT.Data-signal, R1.Pin_1
  N2: Componente2.GND, DHT.GND_1, DHT.GND_2
  N3: Componente2.A0, RL1.Pin_1
  N4: Componente2.A1, RL2.Pin_1
  N5: Componente2.A2, RL3.Pin_1
  5V: Componente2.5V, DHT.Vcc, R1.Pin_0, R2.Pin_0, R4.Pin_0, R6.Pin_0, RL2.Pin_0, RL3.Pin_0, RL1.Pin_0
  N6: R2.Pin_1, R3.Pin_1
  N7: R4.Pin_1, R5.Pin_1
  N8: R6.Pin_1, R7.Pin_1

notes:
  Shinyei
  RTC
  2710
  5521
  2611
  12V
  GND
